# Fritzing sketch dmx_pico_connection (saved by Fritzing 0.9.3b)

parts:
  Mod1 = Raspberry Pi Pico
  RS485_module1 = RS485 Module (MAX3485)
  XLR1 = XLR3_NCFAH2 [package=xlr3_nc3fah2]

nets:
  N1: Mod1.pin_1, RS485_module1.DI
  N2: Mod1.pin_19, RS485_module1.DE
  N3: Mod1.pin_33, Mod1.pin_38, Mod1.pin_42, RS485_module1.GND, XLR1.1
  N4: Mod1.pin_40, RS485_module1.VCC
  N5: RS485_module1.A, XLR1.3
  N6: RS485_module1.B, XLR1.2

notes:
  A - 2
  B - 1
  Gnd - 3
  DMX connector
  MAX485

custom parts:
  Raspberry Pi Pico: Raspberry Pi Pico. Based around the RP2040 microcontroller the Pico is a low cost microcontroller device bringing Raspberry Pi quality, cost, and easy of use to the microcontroller space. Jan 2021, Split part in to two versions: tht (this one) and SMD. This one will drill holes for a .1 in header in pcb to allow plugging in the module as well as providing pads to solder the module to the top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
  RS485 Module (MAX3485): Commercially available RS485 to RS232 TTL Module
